// Logisim project All_Circuits.circ as structural Verilog: 10 circuits, main circuit meioSomador
module meioSomador (
  input  A,
  input  B,
  output meiaSoma,
  output meioVai1
);

  xor xor_1 (meiaSoma, A, B);
  and and_1 (meioVai1, A, B);
endmodule

module Somador1Bit (
  input  Vem1,
  input  A,
  input  B,
  output Soma1,
  output Vai1
);

  wire and_1_out, and_2_out, xor_1_out;

  xor xor_1 (xor_1_out, A, B);
  and and_1 (and_1_out, A, B);
  xor xor_2 (Soma1, Vem1, xor_1_out);
  and and_2 (and_2_out, Vem1, xor_1_out);
  or or_1 (Vai1, and_2_out, and_1_out);
endmodule

module Somador4Bits (
  input  x0,
  input  x1,
  input  x2,
  input  x3,
  input  y0,
  input  y1,
  input  y2,
  input  y3,
  input  Vem1,
  output Overflow,
  output out_11,
  output out_12,
  output out_13,
  output out_14
);

  wire somador1bit_1_vai1, somador1bit_2_vai1, somador1bit_3_vai1, somador1bit_4_vai1;

  Exeperiencia01_Somador1Bit somador1bit_1 (.Vem1(Vem1), .A(x0), .B(y0), .Soma1(out_11), .Vai1(somador1bit_1_vai1));
  Exeperiencia01_Somador1Bit somador1bit_2 (
    .Vem1(somador1bit_1_vai1), .A(x1), .B(y1), .Soma1(out_12), .Vai1(somador1bit_2_vai1));
  Exeperiencia01_Somador1Bit somador1bit_3 (
    .Vem1(somador1bit_2_vai1), .A(x2), .B(y2), .Soma1(out_13), .Vai1(somador1bit_3_vai1));
  Exeperiencia01_Somador1Bit somador1bit_4 (
    .Vem1(somador1bit_3_vai1), .A(x3), .B(y3), .Soma1(out_14), .Vai1(somador1bit_4_vai1));
  xor xor_1 (Overflow, somador1bit_3_vai1, somador1bit_4_vai1);
endmodule

module meu_decotificador (
  input  x0,
  input  x1,
  input  x2,
  input  x3,
  output a,
  output b,
  output c,
  output d,
  output e,
  output f,
  output g
);

  wire and_1_out, and_2_out, and_3_out, and_4_out, and_5_out, and_6_out, and_7_out, and_8_out, and_9_out,
       and_10_out, and_11_out, and_12_out, and_13_out, and_14_out, and_15_out, and_16_out, and_17_out,
       and_18_out, and_19_out, and_20_out, and_21_out, and_22_out, and_23_out, and_24_out, and_25_out,
       and_26_out, and_27_out, and_28_out, and_29_out, and_30_out, and_31_out, and_32_out, and_33_out,
       and_34_out, and_35_out, and_36_out, and_37_out, and_38_out, and_39_out, and_40_out, and_41_out,
       and_42_out, and_43_out, and_44_out, and_45_out, and_46_out, and_47_out, and_48_out, and_49_out,
       and_50_out, not_1_out, not_2_out, not_3_out, not_4_out, not_5_out, not_6_out, not_7_out, not_8_out,
       not_9_out, not_10_out, not_11_out, not_12_out, not_13_out, not_14_out, not_15_out, not_16_out,
       not_17_out, not_18_out, not_19_out, not_20_out, not_21_out, not_22_out, not_23_out, not_24_out,
       not_25_out, not_26_out, not_27_out, not_28_out, not_29_out, not_30_out, not_31_out, not_32_out,
       not_33_out, not_34_out, not_35_out, not_36_out, not_37_out, not_38_out, or_1_out, or_2_out, or_3_out,
       or_4_out, or_5_out, or_6_out, or_7_out, or_9_out, or_11_out, or_12_out, or_13_out, or_14_out,
       or_15_out, or_16_out, or_17_out, or_18_out, or_19_out, or_20_out, or_21_out;

  not not_1 (not_1_out, x0);
  not not_2 (not_2_out, x0);
  and and_1 (and_1_out, not_2_out, x1);
  not not_3 (not_3_out, x1);
  not not_4 (not_4_out, x1);
  and and_2 (and_2_out, not_4_out, not_5_out);
  not not_5 (not_5_out, x2);
  not not_6 (not_6_out, x1);
  and and_3 (and_3_out, not_6_out, x2);
  not not_7 (not_7_out, x3);
  not not_8 (not_8_out, x0);
  not not_9 (not_9_out, x2);
  not not_10 (not_10_out, x3);
  not not_11 (not_11_out, x0);
  and and_4 (and_4_out, not_11_out, x1);
  and and_5 (and_5_out, x2, x3);
  and and_6 (and_6_out, x0, not_12_out);
  not not_12 (not_12_out, x1);
  not not_13 (not_13_out, x2);
  not not_14 (not_14_out, x2);
  not not_15 (not_15_out, x2);
  and and_7 (and_7_out, not_15_out, x3);
  not not_16 (not_16_out, x0);
  and and_8 (and_8_out, not_16_out, x1);
  not not_17 (not_17_out, x1);
  not not_18 (not_18_out, x0);
  and and_9 (and_9_out, not_18_out, not_19_out);
  not not_19 (not_19_out, x1);
  and and_10 (and_10_out, x1, not_20_out);
  not not_20 (not_20_out, x2);
  not not_21 (not_21_out, x1);
  not not_22 (not_22_out, x1);
  and and_11 (and_11_out, not_22_out, x2);
  and and_12 (and_12_out, x2, not_23_out);
  not not_23 (not_23_out, x3);
  and and_13 (and_13_out, x0, not_24_out);
  not not_24 (not_24_out, x3);
  and and_14 (and_14_out, x0, x1);
  not not_25 (not_25_out, x1);
  and and_15 (and_15_out, not_25_out, x2);
  not not_26 (not_26_out, x0);
  and and_16 (and_16_out, not_26_out, x1);
  not not_27 (not_27_out, x2);
  not not_28 (not_28_out, x1);
  and and_17 (and_17_out, not_28_out, x2);
  and and_18 (and_18_out, x2, not_29_out);
  not not_29 (not_29_out, x3);
  not not_30 (not_30_out, x0);
  and and_19 (and_19_out, not_30_out, x1);
  not not_31 (not_31_out, x2);
  not not_32 (not_32_out, x1);
  and and_20 (and_20_out, not_1_out, x2);
  and and_21 (and_21_out, and_1_out, x3);
  and and_22 (and_22_out, x0, not_3_out);
  not not_33 (not_33_out, x2);
  not not_34 (not_34_out, x3);
  and and_23 (and_23_out, and_2_out, x3);
  and and_24 (and_24_out, and_3_out, not_7_out);
  and and_25 (and_25_out, not_8_out, x1);
  and and_26 (and_26_out, not_9_out, not_10_out);
  and and_27 (and_27_out, and_4_out, and_5_out);
  and and_28 (and_28_out, and_6_out, not_13_out);
  and and_29 (and_29_out, x0, not_14_out);
  or or_1 (or_1_out, and_7_out, and_8_out);
  and and_30 (and_30_out, x0, not_17_out);
  and and_31 (and_31_out, and_9_out, x2);
  and and_32 (and_32_out, and_10_out, x3);
  and and_33 (and_33_out, x1, x2);
  not not_35 (not_35_out, x3);
  not not_36 (not_36_out, x2);
  and and_34 (and_34_out, x0, not_21_out);
  or or_2 (or_2_out, and_11_out, and_12_out);
  or or_3 (or_3_out, and_13_out, and_14_out);
  and and_35 (and_35_out, and_15_out, x3);
  and and_36 (and_36_out, and_16_out, not_27_out);
  not not_37 (not_37_out, x3);
  not not_38 (not_38_out, x1);
  or or_4 (or_4_out, and_17_out, and_18_out);
  and and_37 (and_37_out, and_19_out, not_31_out);
  and and_38 (and_38_out, x0, not_32_out);
  and and_39 (and_39_out, x0, x3);
  or or_5 (or_5_out, and_20_out, and_21_out);
  and and_40 (and_40_out, x1, x2);
  and and_41 (and_41_out, and_22_out, not_33_out);
  and and_42 (and_42_out, x0, not_34_out);
  or or_6 (or_6_out, and_23_out, and_24_out);
  and and_43 (and_43_out, and_25_out, and_26_out);
  or or_7 (or_7_out, and_27_out, and_28_out);
  and and_44 (and_44_out, and_29_out, x3);
  or or_8 (c, or_1_out, and_30_out);
  or or_9 (or_9_out, and_31_out, and_32_out);
  and and_45 (and_45_out, and_33_out, not_35_out);
  and and_46 (and_46_out, x0, not_36_out);
  and and_47 (and_47_out, and_34_out, x3);
  or or_10 (e, or_2_out, or_3_out);
  or or_11 (or_11_out, and_35_out, and_36_out);
  and and_48 (and_48_out, x1, not_37_out);
  and and_49 (and_49_out, x0, not_38_out);
  and and_50 (and_50_out, x0, x2);
  or or_12 (or_12_out, or_4_out, and_37_out);
  or or_13 (or_13_out, and_38_out, and_39_out);
  or or_14 (or_14_out, or_5_out, and_40_out);
  or or_15 (or_15_out, and_41_out, and_42_out);
  or or_16 (or_16_out, or_6_out, and_43_out);
  or or_17 (or_17_out, or_7_out, and_44_out);
  or or_18 (or_18_out, or_9_out, and_45_out);
  or or_19 (or_19_out, and_46_out, and_47_out);
  or or_20 (or_20_out, or_11_out, and_48_out);
  or or_21 (or_21_out, and_49_out, and_50_out);
  or or_22 (g, or_12_out, or_13_out);
  or or_23 (a, or_14_out, or_15_out);
  or or_24 (b, or_16_out, or_17_out);
  or or_25 (d, or_18_out, or_19_out);
  or or_26 (f, or_20_out, or_21_out);
endmodule

module Acender_Numero (
  input  b,
  input  a,
  input  f,
  input  g,
  input  e,
  input  d,
  input  c
);

  _7_Segment_Display u_7_segment_display_1 (.g(g), .f(f), .a(a), .b(b), .e(e), .d(d), .c(c));  // open: dp
endmodule

module Mux_00 (
  input  A,
  input  B,
  input  C,
  input  D,
  input  OP1,
  input  OP2,
  output Saida
);

  wire and_1_out, and_2_out, and_3_out, and_4_out, not_1_out, not_2_out, not_3_out, not_4_out;

  not not_1 (not_1_out, OP1);
  not not_2 (not_2_out, OP2);
  not not_3 (not_3_out, OP1);
  not not_4 (not_4_out, OP2);
  and and_1 (and_1_out, A, not_1_out, not_2_out);
  and and_2 (and_2_out, B, not_3_out, OP2);
  and and_3 (and_3_out, C, OP1, not_4_out);
  and and_4 (and_4_out, D, OP1, OP2);
  or or_1 (Saida, and_1_out, and_2_out, and_3_out, and_4_out);
endmodule

module Mux_B_Inverte (
  input  A,
  input  B,
  input  OP1,
  output Saida
);

  wire and_1_out, and_2_out, not_1_out;

  not not_1 (not_1_out, OP1);
  and and_1 (and_1_out, A, not_1_out);
  and and_2 (and_2_out, B, OP1);
  or or_1 (Saida, and_1_out, and_2_out);
endmodule

module ALU_00 (
  input  Carry_In,
  input  Binverte,
  input  A,
  input  B,
  input  OP_0,
  input  OP_1,
  output Result,
  output Carry_Out
);

  wire and_1_out, mux01_1_saida, not_1_out, not_2_out, or_1_out, somador1bit_1_soma1;

  not not_1 (not_1_out, B);
  mux01 mux01_1 (.A(B), .B(not_1_out), .OP1(Binverte), .Saida(mux01_1_saida));
  and and_1 (and_1_out, A, mux01_1_saida);
  or or_1 (or_1_out, A, mux01_1_saida);
  not not_2 (not_2_out, A);
  Exeperiencia01_Somador1Bit somador1bit_1 (
    .Vem1(Carry_In), .A(A), .B(mux01_1_saida), .Soma1(somador1bit_1_soma1), .Vai1(Carry_Out));
  mux00 mux00_1 (
    .A(and_1_out), .B(or_1_out), .C(not_2_out), .D(somador1bit_1_soma1), .OP1(OP_0), .OP2(OP_1),
    .Saida(Result));
endmodule

module ALU_00_4Bits (
  input  A_00,
  input  A_01,
  input  A_02,
  input  A_03,
  input  B_00,
  input  B_01,
  input  B_02,
  input  B_03,
  input  OP_00,
  input  Binverte,
  input  CarryIn,
  input  OP_01,
  output Saida_00,
  output Saida_01,
  output Saida_02,
  output Saida_03,
  output CarryOut
);

  wire alu_01_1_carry_out, alu_01_2_carry_out, alu_01_3_carry_out;

  ALU_01 alu_01_1 (
    .A(A_00), .B(B_00), .OP_0(OP_00), .Binverte(Binverte), .Carry_In(CarryIn),
    .Carry_Out(alu_01_1_carry_out), .Result(Saida_00), .OP_1(OP_01));
  ALU_01 alu_01_2 (
    .A(A_01), .B(B_01), .OP_0(OP_00), .Binverte(Binverte), .Carry_In(alu_01_1_carry_out),
    .Carry_Out(alu_01_2_carry_out), .Result(Saida_01), .OP_1(OP_01));
  ALU_01 alu_01_3 (
    .A(A_02), .B(B_02), .OP_0(OP_00), .Binverte(Binverte), .Carry_In(alu_01_2_carry_out),
    .Carry_Out(alu_01_3_carry_out), .Result(Saida_02), .OP_1(OP_01));
  ALU_01 alu_01_4 (
    .A(A_03), .B(B_03), .OP_0(OP_00), .Binverte(Binverte), .Carry_In(alu_01_3_carry_out),
    .Carry_Out(CarryOut), .Result(Saida_03), .OP_1(OP_01));
endmodule

module ULA (
  input  [3:0] A,
  input  [3:0] B,
  input  [3:0] in_3,
  output [3:0] out_4
);

  wire [3:0] and_1_out, and_2_out, and_3_out, nand_1_out, nor_1_out, not_1_out, not_2_out, not_3_out,
       not_4_out, not_5_out, not_6_out, not_7_out, or_1_out, or_2_out, or_3_out, xor_1_out, xor_2_out;

  assign not_1_out = ~A;  // NOT_Gate not_1, 4 bits wide
  assign not_2_out = ~B;  // NOT_Gate not_2, 4 bits wide
  assign not_3_out = ~A;  // NOT_Gate not_3, 4 bits wide
  assign not_4_out = ~B;  // NOT_Gate not_4, 4 bits wide
  assign not_5_out = ~A;  // NOT_Gate not_5, 4 bits wide
  assign nor_1_out = ~(A | B);  // NOR_Gate nor_1, 4 bits wide
  assign and_1_out = not_1_out & B;  // AND_Gate and_1, 4 bits wide
  assign nand_1_out = ~(A & B);  // NAND_Gate nand_1, 4 bits wide
  assign not_6_out = ~B;  // NOT_Gate not_6, 4 bits wide
  assign xor_1_out = A ^ B;  // XOR_Gate xor_1, 4 bits wide
  assign and_2_out = A & not_2_out;  // AND_Gate and_2, 4 bits wide
  assign or_1_out = not_3_out | B;  // OR_Gate or_1, 4 bits wide
  assign xor_2_out = A ^ B;  // XOR_Gate xor_2, 4 bits wide
  assign and_3_out = A & B;  // AND_Gate and_3, 4 bits wide
  assign or_2_out = A | not_4_out;  // OR_Gate or_2, 4 bits wide
  assign or_3_out = A | B;  // OR_Gate or_3, 4 bits wide
  assign not_7_out = ~xor_2_out;  // NOT_Gate not_7, 4 bits wide
  Multiplexer #(.select(4), .width(4)) multiplexer_1 (
    .in0(not_5_out), .in1(nor_1_out), .in2(and_1_out), .in3(4'b0000), .in4(nand_1_out), .in5(not_6_out),
    .in6(xor_1_out), .in7(and_2_out), .in8(or_1_out), .in9(not_7_out), .in10(B), .in11(and_3_out),
    .in12(4'b1111), .in13(or_2_out), .in14(or_3_out), .in15(A), .out(out_4), .sel(in_3));  // open: en
endmodule
