// Logisim project Exp03.circ as structural Verilog: 1 circuit, main circuit ALU
module ALU (
  input  B_Inverte,
  input  CarryIn,
  input  A,
  input  B,
  input  OP1,
  input  OP0,
  output Saida,
  output CarryOut
);

  wire and_1_out, mux2_1_saida, not_1_out, not_2_out, or_1_out, somador1bit_1_soma1;

  and and_1 (and_1_out, A, B);
  or or_1 (or_1_out, A, B);
  not not_1 (not_1_out, A);
  mux2 mux2_1 (.A(B), .B(not_2_out), .OP1(B_Inverte), .Saida(mux2_1_saida));
  not not_2 (not_2_out, B);
  Somador1Bit somador1bit_1 (.Vem1(A), .A(mux2_1_saida), .B(CarryIn), .Soma1(somador1bit_1_soma1), .Vai1(CarryOut));
  mux mux_1 (.A(and_1_out), .B(or_1_out), .C(not_1_out), .D(somador1bit_1_soma1), .OP1(OP1), .OP2(OP0), .Saida(Saida));
endmodule
