// Logisim project Experiencia02.circ as structural Verilog: 2 circuits, main circuit mux
module mux (
  input  A,
  input  B,
  input  C,
  input  D,
  input  OP1,
  input  OP2,
  output Saida
);

  wire and_1_out, and_2_out, and_3_out, and_4_out, not_1_out, not_2_out, not_3_out, not_4_out;

  not not_1 (not_1_out, OP1);
  not not_2 (not_2_out, OP2);
  not not_3 (not_3_out, OP1);
  not not_4 (not_4_out, OP2);
  and and_1 (and_1_out, A, not_1_out, not_2_out);
  and and_2 (and_2_out, B, not_3_out, OP2);
  and and_3 (and_3_out, C, OP1, not_4_out);
  and and_4 (and_4_out, D, OP1, OP2);
  or or_1 (Saida, and_1_out, and_2_out, and_3_out, and_4_out);
endmodule

module mux2 (
  input  A,
  input  B,
  input  OP1,
  output Saida
);

  wire and_1_out, and_2_out, not_1_out;

  not not_1 (not_1_out, OP1);
  and and_1 (and_1_out, A, not_1_out);
  and and_2 (and_2_out, B, OP1);
  or or_1 (Saida, and_1_out, and_2_out);
endmodule
