// Logisim project Rel_02a.circ as structural Verilog: 2 circuits, main circuit meu decotificador
module meu_decotificador (
  input  x0,
  input  x1,
  input  x2,
  input  x3,
  output a,
  output b,
  output c,
  output d,
  output e,
  output f,
  output g
);

  wire and_1_out, and_2_out, and_3_out, and_4_out, and_5_out, and_6_out, and_7_out, and_8_out, and_9_out,
       and_10_out, and_11_out, and_12_out, and_13_out, and_14_out, and_15_out, and_16_out, and_17_out,
       and_18_out, and_19_out, and_20_out, and_21_out, and_22_out, and_23_out, and_24_out, and_25_out,
       and_26_out, and_27_out, and_28_out, and_29_out, and_30_out, and_31_out, and_32_out, and_33_out,
       and_34_out, and_35_out, and_36_out, and_37_out, and_38_out, and_39_out, and_40_out, and_41_out,
       and_42_out, and_43_out, and_44_out, and_45_out, and_46_out, and_47_out, and_48_out, and_49_out,
       and_50_out, not_1_out, not_2_out, not_3_out, not_4_out, not_5_out, not_6_out, not_7_out, not_8_out,
       not_9_out, not_10_out, not_11_out, not_12_out, not_13_out, not_14_out, not_15_out, not_16_out,
       not_17_out, not_18_out, not_19_out, not_20_out, not_21_out, not_22_out, not_23_out, not_24_out,
       not_25_out, not_26_out, not_27_out, not_28_out, not_29_out, not_30_out, not_31_out, not_32_out,
       not_33_out, not_34_out, not_35_out, not_36_out, not_37_out, not_38_out, or_1_out, or_2_out, or_3_out,
       or_4_out, or_5_out, or_6_out, or_7_out, or_9_out, or_11_out, or_12_out, or_13_out, or_14_out,
       or_15_out, or_16_out, or_17_out, or_18_out, or_19_out, or_20_out, or_21_out;

  not not_1 (not_1_out, x0);
  not not_2 (not_2_out, x0);
  and and_1 (and_1_out, not_2_out, x1);
  not not_3 (not_3_out, x1);
  not not_4 (not_4_out, x1);
  and and_2 (and_2_out, not_4_out, not_5_out);
  not not_5 (not_5_out, x2);
  not not_6 (not_6_out, x1);
  and and_3 (and_3_out, not_6_out, x2);
  not not_7 (not_7_out, x3);
  not not_8 (not_8_out, x0);
  not not_9 (not_9_out, x2);
  not not_10 (not_10_out, x3);
  not not_11 (not_11_out, x0);
  and and_4 (and_4_out, not_11_out, x1);
  and and_5 (and_5_out, x2, x3);
  and and_6 (and_6_out, x0, not_12_out);
  not not_12 (not_12_out, x1);
  not not_13 (not_13_out, x2);
  not not_14 (not_14_out, x2);
  not not_15 (not_15_out, x2);
  and and_7 (and_7_out, not_15_out, x3);
  not not_16 (not_16_out, x0);
  and and_8 (and_8_out, not_16_out, x1);
  not not_17 (not_17_out, x1);
  not not_18 (not_18_out, x0);
  and and_9 (and_9_out, not_18_out, not_19_out);
  not not_19 (not_19_out, x1);
  and and_10 (and_10_out, x1, not_20_out);
  not not_20 (not_20_out, x2);
  not not_21 (not_21_out, x1);
  not not_22 (not_22_out, x1);
  and and_11 (and_11_out, not_22_out, x2);
  and and_12 (and_12_out, x2, not_23_out);
  not not_23 (not_23_out, x3);
  and and_13 (and_13_out, x0, not_24_out);
  not not_24 (not_24_out, x3);
  and and_14 (and_14_out, x0, x1);
  not not_25 (not_25_out, x1);
  and and_15 (and_15_out, not_25_out, x2);
  not not_26 (not_26_out, x0);
  and and_16 (and_16_out, not_26_out, x1);
  not not_27 (not_27_out, x2);
  not not_28 (not_28_out, x1);
  and and_17 (and_17_out, not_28_out, x2);
  and and_18 (and_18_out, x2, not_29_out);
  not not_29 (not_29_out, x3);
  not not_30 (not_30_out, x0);
  and and_19 (and_19_out, not_30_out, x1);
  not not_31 (not_31_out, x2);
  not not_32 (not_32_out, x1);
  and and_20 (and_20_out, not_1_out, x2);
  and and_21 (and_21_out, and_1_out, x3);
  and and_22 (and_22_out, x0, not_3_out);
  not not_33 (not_33_out, x2);
  not not_34 (not_34_out, x3);
  and and_23 (and_23_out, and_2_out, x3);
  and and_24 (and_24_out, and_3_out, not_7_out);
  and and_25 (and_25_out, not_8_out, x1);
  and and_26 (and_26_out, not_9_out, not_10_out);
  and and_27 (and_27_out, and_4_out, and_5_out);
  and and_28 (and_28_out, and_6_out, not_13_out);
  and and_29 (and_29_out, x0, not_14_out);
  or or_1 (or_1_out, and_7_out, and_8_out);
  and and_30 (and_30_out, x0, not_17_out);
  and and_31 (and_31_out, and_9_out, x2);
  and and_32 (and_32_out, and_10_out, x3);
  and and_33 (and_33_out, x1, x2);
  not not_35 (not_35_out, x3);
  not not_36 (not_36_out, x2);
  and and_34 (and_34_out, x0, not_21_out);
  or or_2 (or_2_out, and_11_out, and_12_out);
  or or_3 (or_3_out, and_13_out, and_14_out);
  and and_35 (and_35_out, and_15_out, x3);
  and and_36 (and_36_out, and_16_out, not_27_out);
  not not_37 (not_37_out, x3);
  not not_38 (not_38_out, x1);
  or or_4 (or_4_out, and_17_out, and_18_out);
  and and_37 (and_37_out, and_19_out, not_31_out);
  and and_38 (and_38_out, x0, not_32_out);
  and and_39 (and_39_out, x0, x3);
  or or_5 (or_5_out, and_20_out, and_21_out);
  and and_40 (and_40_out, x1, x2);
  and and_41 (and_41_out, and_22_out, not_33_out);
  and and_42 (and_42_out, x0, not_34_out);
  or or_6 (or_6_out, and_23_out, and_24_out);
  and and_43 (and_43_out, and_25_out, and_26_out);
  or or_7 (or_7_out, and_27_out, and_28_out);
  and and_44 (and_44_out, and_29_out, x3);
  or or_8 (c, or_1_out, and_30_out);
  or or_9 (or_9_out, and_31_out, and_32_out);
  and and_45 (and_45_out, and_33_out, not_35_out);
  and and_46 (and_46_out, x0, not_36_out);
  and and_47 (and_47_out, and_34_out, x3);
  or or_10 (e, or_2_out, or_3_out);
  or or_11 (or_11_out, and_35_out, and_36_out);
  and and_48 (and_48_out, x1, not_37_out);
  and and_49 (and_49_out, x0, not_38_out);
  and and_50 (and_50_out, x0, x2);
  or or_12 (or_12_out, or_4_out, and_37_out);
  or or_13 (or_13_out, and_38_out, and_39_out);
  or or_14 (or_14_out, or_5_out, and_40_out);
  or or_15 (or_15_out, and_41_out, and_42_out);
  or or_16 (or_16_out, or_6_out, and_43_out);
  or or_17 (or_17_out, or_7_out, and_44_out);
  or or_18 (or_18_out, or_9_out, and_45_out);
  or or_19 (or_19_out, and_46_out, and_47_out);
  or or_20 (or_20_out, or_11_out, and_48_out);
  or or_21 (or_21_out, and_49_out, and_50_out);
  or or_22 (g, or_12_out, or_13_out);
  or or_23 (a, or_14_out, or_15_out);
  or or_24 (b, or_16_out, or_17_out);
  or or_25 (d, or_18_out, or_19_out);
  or or_26 (f, or_20_out, or_21_out);
endmodule

module main (
  input  b,
  input  a,
  input  f,
  input  g,
  input  e,
  input  d,
  input  c
);

  _7_Segment_Display u_7_segment_display_1 (.g(g), .f(f), .a(a), .b(b), .e(e), .d(d), .c(c));  // open: dp
endmodule
