// Logisim project deafdb6d-ab20-49bf-b589-8af71ad7adfa_1520393_P1_Cora Silberschneider.circ as structural Verilog: 3 circuits, main circuit main
module main (
  input  a3,
  input  a2,
  input  a1,
  input  a0,
  input  b3,
  input  b2,
  input  b1,
  input  b0,
  output P7,
  output P6,
  output P5,
  output P4,
  output P3,
  output P2,
  output P1,
  output P0
);

  wire and_1_out, and_2_out, and_3_out, and_4_out, and_5_out, and_6_out, and_7_out, and_8_out, and_9_out,
       and_10_out, and_11_out, and_12_out, and_13_out, and_14_out, and_15_out, somador_1_bit_2_vai1,
       somador_1_bit_3_soma, somador_1_bit_3_vai1, somador_1_bit_4_soma, somador_1_bit_4_vai1,
       somador_1_bit_5_vai1, somador_1_bit_6_soma, somador_1_bit_6_vai1, somador_1_bit_7_vai1,
       somador_1_bit_8_soma, somador_1_bit_8_vai1, somador_1_bit_9_soma, somador_1_bit_9_vai1,
       somador_1_bit_10_soma, somador_1_bit_10_vai1, somador_1_bit_11_vai1, somador_1_bit_12_soma,
       somador_1_bit_12_vai1, somador_1_bit_13_soma, somador_1_bit_13_vai1, somador_1_bit_14_vai1;

  and and_1 (and_1_out, b3, a3);
  Somador_1_bit somador_1_bit_1 (.vem1(1'b0), .x(somador_1_bit_2_vai1), .y(and_1_out), .soma(P6), .vai1(P7));
  and and_2 (and_2_out, b3, a2);
  Somador_1_bit somador_1_bit_2 (
    .vem1(somador_1_bit_3_vai1), .x(somador_1_bit_3_soma), .y(and_2_out), .soma(P5),
    .vai1(somador_1_bit_2_vai1));
  and and_3 (and_3_out, b2, a3);
  Somador_1_bit somador_1_bit_3 (
    .vem1(1'b0), .x(somador_1_bit_5_vai1), .y(and_3_out), .soma(somador_1_bit_3_soma),
    .vai1(somador_1_bit_3_vai1));
  and and_4 (and_4_out, b3, a1);
  and and_5 (and_5_out, b2, a2);
  Somador_1_bit somador_1_bit_4 (
    .vem1(somador_1_bit_6_vai1), .x(somador_1_bit_6_soma), .y(and_5_out), .soma(somador_1_bit_4_soma),
    .vai1(somador_1_bit_4_vai1));
  Somador_1_bit somador_1_bit_5 (
    .vem1(somador_1_bit_4_vai1), .x(somador_1_bit_4_soma), .y(and_4_out), .soma(P4),
    .vai1(somador_1_bit_5_vai1));
  and and_6 (and_6_out, b1, a3);
  Somador_1_bit somador_1_bit_6 (
    .vem1(1'b0), .x(somador_1_bit_7_vai1), .y(and_6_out), .soma(somador_1_bit_6_soma),
    .vai1(somador_1_bit_6_vai1));
  and and_7 (and_7_out, b3, a0);
  Somador_1_bit somador_1_bit_7 (
    .vem1(somador_1_bit_8_vai1), .x(somador_1_bit_8_soma), .y(and_7_out), .soma(P3),
    .vai1(somador_1_bit_7_vai1));
  and and_8 (and_8_out, b2, a1);
  Somador_1_bit somador_1_bit_8 (
    .vem1(somador_1_bit_10_vai1), .x(somador_1_bit_10_soma), .y(and_8_out), .soma(somador_1_bit_8_soma),
    .vai1(somador_1_bit_8_vai1));
  and and_9 (and_9_out, b0, a3);
  and and_10 (and_10_out, b1, a2);
  Somador_1_bit somador_1_bit_9 (
    .vem1(1'b0), .x(somador_1_bit_11_vai1), .y(and_9_out), .soma(somador_1_bit_9_soma),
    .vai1(somador_1_bit_9_vai1));
  Somador_1_bit somador_1_bit_10 (
    .vem1(somador_1_bit_9_vai1), .x(somador_1_bit_9_soma), .y(and_10_out), .soma(somador_1_bit_10_soma),
    .vai1(somador_1_bit_10_vai1));
  Somador_1_bit somador_1_bit_11 (
    .vem1(somador_1_bit_14_vai1), .x(somador_1_bit_12_vai1), .y(somador_1_bit_12_soma), .soma(P2),
    .vai1(somador_1_bit_11_vai1));
  and and_11 (and_11_out, b2, a0);
  and and_12 (and_12_out, b1, a1);
  Somador_1_bit somador_1_bit_12 (
    .vem1(somador_1_bit_13_vai1), .x(somador_1_bit_13_soma), .y(and_11_out), .soma(somador_1_bit_12_soma),
    .vai1(somador_1_bit_12_vai1));
  and and_13 (and_13_out, b0, a2);
  Somador_1_bit somador_1_bit_13 (
    .vem1(1'b0), .x(and_13_out), .y(and_12_out), .soma(somador_1_bit_13_soma), .vai1(somador_1_bit_13_vai1));
  and and_14 (and_14_out, a0, b1);
  and and_15 (and_15_out, b0, a1);
  Somador_1_bit somador_1_bit_14 (.vem1(1'b0), .x(and_15_out), .y(and_14_out), .soma(P1), .vai1(somador_1_bit_14_vai1));
  and and_16 (P0, b0, a0);
endmodule

module Meio_Somador (
  input  A,
  input  B,
  output meiaSoma,
  output meioVai1
);

  and and_1 (meioVai1, B, A);
  xor xor_1 (meiaSoma, A, B);
endmodule

module Somador_1_bit (
  input  vem1,
  input  x,
  input  y,
  output soma,
  output vai1
);

  wire meio_somador_1_meiasoma, meio_somador_1_meiovai1, meio_somador_2_meiovai1;

  Meio_Somador meio_somador_1 (.A(x), .B(y), .meiaSoma(meio_somador_1_meiasoma), .meioVai1(meio_somador_1_meiovai1));
  Meio_Somador meio_somador_2 (
    .A(vem1), .B(meio_somador_1_meiasoma), .meiaSoma(soma), .meioVai1(meio_somador_2_meiovai1));
  or or_1 (vai1, meio_somador_2_meiovai1, meio_somador_1_meiovai1);
endmodule
